// Logisim project Substractor4bits.circ as structural Verilog: 3 circuits, main circuit main
module main (
  input  A3,
  input  B3,
  input  A2,
  input  B2,
  input  A1,
  input  B1,
  input  A0,
  input  B0,
  input  T,
  output Cout,
  output Overflow,
  output out_12,
  output out_13,
  output out_14,
  output out_15
);

  wire xor_1_out, xor_2_out, xor_3_out, xor_4_out;

  xor xor_1 (xor_1_out, B3, T);
  xor xor_2 (xor_2_out, B2, T);
  xor xor_3 (xor_3_out, B1, T);
  xor xor_4 (xor_4_out, B0, T);
  _4bitFullAdder u_4bitfulladder_1 (
    .Cout(Cout), .b1(xor_4_out), .a1(A0), .b2(xor_3_out), .a2(A1), .b3(xor_2_out), .a3(A2), .b4(xor_1_out),
    .a4(A3), .sum1(out_15), .sum2(out_14), .sum3(out_13), .sum4(out_12), .Cin(T), .Overflow(Overflow));

  // Notes on the sheet:
  //   Complementing switch
  //   1->substract, 0->add
endmodule

module FullAdderCircuit (
  input  A,
  input  B,
  input  Cin,
  output Sum,
  output Cout
);

  wire and_1_out, and_2_out, xor_1_out;

  xor xor_1 (xor_1_out, A, B);
  xor xor_2 (Sum, xor_1_out, Cin);
  and and_1 (and_1_out, xor_1_out, Cin);
  and and_2 (and_2_out, A, B);
  or or_1 (Cout, and_1_out, and_2_out);
endmodule

module _4bitFullAdder (
  input  Cin,
  input  b1,
  input  a1,
  input  b2,
  input  a2,
  input  b3,
  input  a3,
  input  b4,
  input  a4,
  output Cout,
  output Overflow,
  output sum1,
  output sum2,
  output sum3,
  output sum4
);

  wire fulladdercircuit_1_cout, fulladdercircuit_2_cout, fulladdercircuit_3_cout;

  FullAdderCircuit fulladdercircuit_1 (.A(a1), .B(b1), .Cin(Cin), .Sum(sum1), .Cout(fulladdercircuit_1_cout));
  FullAdderCircuit fulladdercircuit_2 (
    .A(a2), .B(b2), .Cin(fulladdercircuit_1_cout), .Sum(sum2), .Cout(fulladdercircuit_2_cout));
  FullAdderCircuit fulladdercircuit_3 (
    .A(a3), .B(b3), .Cin(fulladdercircuit_2_cout), .Sum(sum3), .Cout(fulladdercircuit_3_cout));
  FullAdderCircuit fulladdercircuit_4 (.A(a4), .B(b4), .Cin(fulladdercircuit_3_cout), .Sum(sum4), .Cout(Cout));
  xor xor_1 (Overflow, Cout, fulladdercircuit_3_cout);
endmodule
