// Logisim project Disenos.circ as structural Verilog: 2 circuits, main circuit main
module main (
);

  wire and_1_out, and_2_out, and_3_out, and_4_out, and_5_out, and_6_out, and_7_out, and_8_out, and_9_out,
       and_10_out, and_11_out, clock_1_out, clock_2_out, j_k_ff_5_q, j_k_ff_7_q, j_k_ff_9_q, j_k_ff_12_q,
       j_k_ff_14_q, j_k_ff_15_q, j_k_ff_16_q, mod10_1_tc, n7seg_encoder_1_a, n7seg_encoder_1_b,
       n7seg_encoder_1_c, n7seg_encoder_1_d, n7seg_encoder_1_e, n7seg_encoder_1_f, n7seg_encoder_1_g,
       n7seg_encoder_2_a, n7seg_encoder_2_b, n7seg_encoder_2_c, n7seg_encoder_2_d, n7seg_encoder_2_e,
       n7seg_encoder_2_f, n7seg_encoder_2_g;
  wire [3:0] j_k_ff_1_q, j_k_ff_6_q;

  Clock clock_1 (.out(clock_1_out));
  J_K_Flip_Flop j_k_ff_1 (
    .J(1'b1), .clk(clock_1_out), .K(1'b1), .Q(j_k_ff_1_q[0]), .en(1'b1), .reset(and_3_out));  // open: Qn, preset
  Clock clock_2 (.out(clock_2_out));
  and and_1 (and_1_out, j_k_ff_1_q[0], j_k_ff_1_q[1]);
  J_K_Flip_Flop j_k_ff_2 (
    .J(j_k_ff_1_q[0]), .clk(clock_1_out), .K(j_k_ff_1_q[0]), .Q(j_k_ff_1_q[1]), .en(1'b1), .reset(and_3_out));  // open: Qn, preset
  J_K_Flip_Flop j_k_ff_3 (
    .J(and_1_out), .clk(clock_1_out), .K(and_1_out), .Q(j_k_ff_1_q[2]), .en(1'b1), .reset(and_3_out));  // open: Qn, preset
  MOD10 mod10_1 (.CLK(clock_2_out), .EN(1'b1), .TC(mod10_1_tc));  // open: _3, _2, _1, _0
  and and_2 (and_2_out, and_1_out, j_k_ff_1_q[2]);
  J_K_Flip_Flop j_k_ff_4 (
    .J(and_2_out), .clk(clock_1_out), .K(and_2_out), .Q(j_k_ff_1_q[3]), .en(1'b1), .reset(and_3_out));  // open: Qn, preset
  J_K_Flip_Flop j_k_ff_5 (
    .J(1'b1), .clk(mod10_1_tc), .K(1'b1), .Q(j_k_ff_5_q), .en(1'b1), .reset(and_7_out));  // open: Qn, preset
  and and_3 (and_3_out, j_k_ff_1_q[1], j_k_ff_1_q[3]);
  J_K_Flip_Flop j_k_ff_6 (
    .J(1'b1), .clk(and_3_out), .K(1'b1), .Q(j_k_ff_6_q[0]), .en(1'b1), .reset(and_9_out));  // open: Qn, preset
  _7_Segment_Display u_7_segment_display_1 (
    .g(n7seg_encoder_1_g), .f(n7seg_encoder_1_f), .a(n7seg_encoder_1_a), .b(n7seg_encoder_1_b),
    .e(n7seg_encoder_1_e), .d(n7seg_encoder_1_d), .c(n7seg_encoder_1_c));  // open: dp
  _7seg_encoder u_7seg_encoder_1 (
    .Input(j_k_ff_6_q), .E(n7seg_encoder_1_e), .D(n7seg_encoder_1_d), .C(n7seg_encoder_1_c),
    .G(n7seg_encoder_1_g), .F(n7seg_encoder_1_f), .A(n7seg_encoder_1_a), .B(n7seg_encoder_1_b));
  and and_4 (and_4_out, j_k_ff_5_q, j_k_ff_7_q);
  J_K_Flip_Flop j_k_ff_7 (
    .J(j_k_ff_5_q), .clk(mod10_1_tc), .K(j_k_ff_5_q), .Q(j_k_ff_7_q), .en(1'b1), .reset(and_7_out));  // open: Qn, preset
  J_K_Flip_Flop j_k_ff_8 (
    .J(j_k_ff_6_q[0]), .clk(and_3_out), .K(j_k_ff_6_q[0]), .Q(j_k_ff_6_q[1]), .en(1'b1), .reset(and_9_out));  // open: Qn, preset
  _7_Segment_Display u_7_segment_display_2 (
    .g(n7seg_encoder_2_g), .f(n7seg_encoder_2_f), .a(n7seg_encoder_2_a), .b(n7seg_encoder_2_b),
    .e(n7seg_encoder_2_e), .d(n7seg_encoder_2_d), .c(n7seg_encoder_2_c));  // open: dp
  _7seg_encoder u_7seg_encoder_2 (
    .Input(j_k_ff_1_q), .E(n7seg_encoder_2_e), .D(n7seg_encoder_2_d), .C(n7seg_encoder_2_c),
    .G(n7seg_encoder_2_g), .F(n7seg_encoder_2_f), .A(n7seg_encoder_2_a), .B(n7seg_encoder_2_b));
  J_K_Flip_Flop j_k_ff_9 (
    .J(and_4_out), .clk(mod10_1_tc), .K(and_4_out), .Q(j_k_ff_9_q), .en(1'b1), .reset(and_7_out));  // open: Qn, preset
  and and_5 (and_5_out, j_k_ff_6_q[0], j_k_ff_6_q[1]);
  and and_6 (and_6_out, and_4_out, j_k_ff_9_q);
  and and_7 (and_7_out, j_k_ff_5_q, j_k_ff_9_q);
  J_K_Flip_Flop j_k_ff_10 (
    .J(and_6_out), .clk(mod10_1_tc), .K(and_6_out), .Q(and_7_out), .en(1'b1), .reset(and_7_out));  // open: Qn, preset
  and and_8 (and_8_out, and_5_out, j_k_ff_6_q[2]);
  J_K_Flip_Flop j_k_ff_11 (
    .J(and_5_out), .clk(and_3_out), .K(and_5_out), .Q(j_k_ff_6_q[2]), .en(1'b1), .reset(and_9_out));  // open: Qn, preset
  J_K_Flip_Flop j_k_ff_12 (
    .J(1'b1), .clk(and_7_out), .K(1'b1), .Q(j_k_ff_12_q), .en(1'b1), .reset(j_k_ff_16_q));  // open: Qn, preset
  and and_9 (and_9_out, j_k_ff_6_q[2], j_k_ff_6_q[0]);
  J_K_Flip_Flop j_k_ff_13 (
    .J(and_8_out), .clk(and_3_out), .K(and_8_out), .Q(j_k_ff_6_q[3]), .en(1'b1), .reset(and_9_out));  // open: Qn, preset
  J_K_Flip_Flop j_k_ff_14 (
    .J(j_k_ff_12_q), .clk(and_7_out), .K(j_k_ff_12_q), .Q(j_k_ff_14_q), .en(1'b1), .reset(j_k_ff_16_q));  // open: Qn, preset
  and and_10 (and_10_out, j_k_ff_12_q, j_k_ff_14_q);
  J_K_Flip_Flop j_k_ff_15 (
    .J(and_10_out), .clk(and_7_out), .K(and_10_out), .Q(j_k_ff_15_q), .en(1'b1), .reset(j_k_ff_16_q));  // open: Qn, preset
  and and_11 (and_11_out, and_10_out, j_k_ff_15_q);
  J_K_Flip_Flop j_k_ff_16 (
    .J(and_11_out), .clk(and_7_out), .K(and_11_out), .Q(j_k_ff_16_q), .en(1'b1), .reset(j_k_ff_16_q));  // open: Qn, preset
endmodule

module MOD10 (
  input  CLK,
  input  EN,
  output TC,
  output _3,
  output _2,
  output _1,
  output _0
);

  wire and_1_out, and_2_out;

  J_K_Flip_Flop j_k_ff_1 (.J(1'b1), .clk(CLK), .K(1'b1), .Q(_0), .en(EN), .reset(TC));  // open: Qn, preset
  J_K_Flip_Flop j_k_ff_2 (.J(_0), .clk(CLK), .K(_0), .Q(_1), .en(EN), .reset(TC));  // open: Qn, preset
  and and_1 (and_1_out, _0, _1);
  J_K_Flip_Flop j_k_ff_3 (.J(and_1_out), .clk(CLK), .K(and_1_out), .Q(_2), .en(EN), .reset(TC));  // open: Qn, preset
  and and_2 (and_2_out, and_1_out, _2);
  and and_3 (TC, _1, _3);
  J_K_Flip_Flop j_k_ff_4 (.J(and_2_out), .clk(CLK), .K(and_2_out), .Q(_3), .en(EN), .reset(TC));  // open: Qn, preset
endmodule
