// Logisim project Examen Parcial.circ as structural Verilog: 2 circuits, main circuit main
module main (
  input  W,
  input  X,
  output M,
  output N,
  output R
);

  wire A_q, A_qn, and_1_out, and_2_out, and_3_out, and_4_out, and_5_out, and_6_out, and_7_out, B_q, B_qn,
       clock_1_out, not_1_out, or_1_out, or_2_out;

  not not_1 (not_1_out, X);
  and and_1 (and_1_out, A_qn, not_1_out);
  and and_2 (and_2_out, A_qn, B_q);
  and and_3 (and_3_out, A_q, B_qn);
  and and_4 (and_4_out, A_q, W);
  and and_5 (and_5_out, B_qn, X);
  and and_6 (and_6_out, A_q, B_qn);
  and and_7 (and_7_out, A_q, W);
  or or_1 (or_1_out, and_1_out, and_2_out, and_3_out, and_4_out);
  or or_2 (or_2_out, and_5_out, and_6_out, and_7_out);
  Clock clock_1 (.out(clock_1_out));
  D_Flip_Flop A (.clk(clock_1_out), .D(or_1_out), .Q(A_q), .Qn(A_qn));  // open: preset, en, reset
  D_Flip_Flop B (.clk(clock_1_out), .D(or_2_out), .Q(B_q), .Qn(B_qn));  // open: preset, en, reset
  and and_8 (M, B_qn, A_qn);
  and and_9 (N, A_q, B_q);
  and and_10 (R, A_qn, B_q);
endmodule

module Examen (
  input  A,
  input  B,
  input  W,
  input  X,
  output A_1,
  output B_1,
  output DA,
  output DB,
  output M,
  output N,
  output R
);

  wire and_1_out, and_2_out, and_3_out, and_4_out, and_5_out, and_6_out, and_7_out, and_8_out, and_9_out,
       and_10_out, and_11_out, and_12_out, and_13_out, and_14_out, not_1_out, not_2_out, not_3_out,
       not_4_out, not_5_out, not_6_out, not_7_out, not_8_out, not_9_out, not_10_out, not_11_out, not_12_out,
       not_13_out, not_14_out, not_15_out;

  not not_1 (not_1_out, A);
  and and_1 (and_1_out, not_1_out, not_2_out);
  not not_2 (not_2_out, X);
  not not_3 (not_3_out, A);
  and and_2 (and_2_out, not_3_out, B);
  and and_3 (and_3_out, A, not_4_out);
  not not_4 (not_4_out, B);
  and and_4 (and_4_out, A, W);
  not not_5 (not_5_out, B);
  and and_5 (and_5_out, not_5_out, X);
  and and_6 (and_6_out, A, not_6_out);
  not not_6 (not_6_out, B);
  and and_7 (and_7_out, A, W);
  not not_7 (not_7_out, A);
  and and_8 (and_8_out, not_7_out, not_8_out);
  not not_8 (not_8_out, X);
  not not_9 (not_9_out, A);
  and and_9 (and_9_out, not_9_out, B);
  and and_10 (and_10_out, A, not_10_out);
  not not_10 (not_10_out, B);
  and and_11 (and_11_out, A, W);
  not not_11 (not_11_out, B);
  and and_12 (and_12_out, not_11_out, X);
  and and_13 (and_13_out, A, not_12_out);
  not not_12 (not_12_out, B);
  and and_14 (and_14_out, A, W);
  not not_13 (not_13_out, A);
  and and_15 (M, not_13_out, not_14_out);
  not not_14 (not_14_out, B);
  and and_16 (N, A, B);
  not not_15 (not_15_out, A);
  and and_17 (R, not_15_out, B);
  or or_1 (A_1, and_1_out, and_2_out, and_3_out, and_4_out);
  or or_2 (B_1, and_5_out, and_6_out, and_7_out);
  or or_3 (DA, and_8_out, and_9_out, and_10_out, and_11_out);
  or or_4 (DB, and_12_out, and_13_out, and_14_out);
endmodule
