// Logisim project Lab4 final esquemático.circ as structural Verilog: 2 circuits, main circuit main
module main (
  input  in_1,
  input  in_2,
  input  in_3,
  input  in_4,
  input  [3:0] B,
  input  in_6
);

  wire and_1_out, clock_1_out, counter_1_carry, flipflop_1_o1, flipflop_1_o2, flipflop_1_o3, flipflop_1_o4,
       flipflop_1_o5, flipflop_1_o6, flipflop_1_o7, flipflop_2_o1, flipflop_2_o2, flipflop_2_o3,
       flipflop_2_o4, flipflop_2_o5, flipflop_2_o6, flipflop_2_o7, flipflop_3_o1, flipflop_3_o2,
       flipflop_3_o3, flipflop_3_o4, flipflop_3_o5, flipflop_3_o6, flipflop_3_o7, flipflop_4_o1,
       flipflop_4_o2, flipflop_4_o3, flipflop_4_o4, flipflop_4_o5, flipflop_4_o6, flipflop_4_o7,
       n7seg_encoder_1_a, n7seg_encoder_1_b, n7seg_encoder_1_c, n7seg_encoder_1_d, n7seg_encoder_1_e,
       n7seg_encoder_1_f, n7seg_encoder_1_g;
  wire [1:0] counter_1_q;
  wire [3:0] multiplexer_1_out;

  _7_Segment_Display u_7_segment_display_1 (
    .g(flipflop_1_o4), .f(flipflop_1_o5), .a(flipflop_1_o6), .b(flipflop_1_o7), .e(flipflop_1_o1),
    .d(flipflop_1_o2), .c(flipflop_1_o3));  // open: dp
  Multiplexer #(.select(2)) multiplexer_1 (
    .in0(B[0]), .in1(B[1]), .in2(B[2]), .in3(B[3]), .out(multiplexer_1_out[0]), .sel(counter_1_q), .en(1'b1));
  flipflop flipflop_1 (
    .CLK(clock_1_out), .I1(n7seg_encoder_1_e), .I2(n7seg_encoder_1_d), .I3(n7seg_encoder_1_c),
    .I4(n7seg_encoder_1_g), .I5(n7seg_encoder_1_f), .I6(n7seg_encoder_1_a), .I7(n7seg_encoder_1_b),
    .Enable(in_1), .O1(flipflop_1_o1), .O2(flipflop_1_o2), .O3(flipflop_1_o3), .O4(flipflop_1_o4),
    .O5(flipflop_1_o5), .O6(flipflop_1_o6), .O7(flipflop_1_o7));
  _7_Segment_Display u_7_segment_display_2 (
    .g(flipflop_2_o4), .f(flipflop_2_o5), .a(flipflop_2_o6), .b(flipflop_2_o7), .e(flipflop_2_o1),
    .d(flipflop_2_o2), .c(flipflop_2_o3));  // open: dp
  flipflop flipflop_2 (
    .CLK(clock_1_out), .I1(n7seg_encoder_1_e), .I2(n7seg_encoder_1_d), .I3(n7seg_encoder_1_c),
    .I4(n7seg_encoder_1_g), .I5(n7seg_encoder_1_f), .I6(n7seg_encoder_1_a), .I7(n7seg_encoder_1_b),
    .Enable(in_2), .O1(flipflop_2_o1), .O2(flipflop_2_o2), .O3(flipflop_2_o3), .O4(flipflop_2_o4),
    .O5(flipflop_2_o5), .O6(flipflop_2_o6), .O7(flipflop_2_o7));
  Clock clock_1 (.out(clock_1_out));
  Counter #(.width(2), .max('h3)) counter_1 (
    .count(1'b1), .Q(counter_1_q), .carry(counter_1_carry), .clk(and_1_out), .clr(in_6));  // open: load, D
  _7_Segment_Display u_7_segment_display_3 (
    .g(flipflop_3_o4), .f(flipflop_3_o5), .a(flipflop_3_o6), .b(flipflop_3_o7), .e(flipflop_3_o1),
    .d(flipflop_3_o2), .c(flipflop_3_o3));  // open: dp
  and and_1 (and_1_out, clock_1_out, ~counter_1_carry);  // AND_Gate
  flipflop flipflop_3 (
    .CLK(clock_1_out), .I1(n7seg_encoder_1_e), .I2(n7seg_encoder_1_d), .I3(n7seg_encoder_1_c),
    .I4(n7seg_encoder_1_g), .I5(n7seg_encoder_1_f), .I6(n7seg_encoder_1_a), .I7(n7seg_encoder_1_b),
    .Enable(in_3), .O1(flipflop_3_o1), .O2(flipflop_3_o2), .O3(flipflop_3_o3), .O4(flipflop_3_o4),
    .O5(flipflop_3_o5), .O6(flipflop_3_o6), .O7(flipflop_3_o7));
  _7_Segment_Display u_7_segment_display_4 (
    .g(flipflop_4_o4), .f(flipflop_4_o5), .a(flipflop_4_o6), .b(flipflop_4_o7), .e(flipflop_4_o1),
    .d(flipflop_4_o2), .c(flipflop_4_o3));  // open: dp
  _7seg_encoder u_7seg_encoder_1 (
    .Input(multiplexer_1_out), .E(n7seg_encoder_1_e), .D(n7seg_encoder_1_d), .C(n7seg_encoder_1_c),
    .G(n7seg_encoder_1_g), .F(n7seg_encoder_1_f), .A(n7seg_encoder_1_a), .B(n7seg_encoder_1_b));
  // serial_main main_1: pin names not known; wires that end beside it: multiplexer_1_out[3], multiplexer_1_out[2], multiplexer_1_out[3], multiplexer_1_out[1], multiplexer_1_out[2], multiplexer_1_out[0], multiplexer_1_out[1], and_1_out, in_6
  flipflop flipflop_4 (
    .CLK(clock_1_out), .I1(n7seg_encoder_1_e), .I2(n7seg_encoder_1_d), .I3(n7seg_encoder_1_c),
    .I4(n7seg_encoder_1_g), .I5(n7seg_encoder_1_f), .I6(n7seg_encoder_1_a), .I7(n7seg_encoder_1_b),
    .Enable(in_4), .O1(flipflop_4_o1), .O2(flipflop_4_o2), .O3(flipflop_4_o3), .O4(flipflop_4_o4),
    .O5(flipflop_4_o5), .O6(flipflop_4_o6), .O7(flipflop_4_o7));
endmodule

module flipflop (
  input  CLK,
  input  I1,
  input  I2,
  input  I3,
  input  I4,
  input  I5,
  input  I6,
  input  I7,
  input  Enable,
  output O1,
  output O2,
  output O3,
  output O4,
  output O5,
  output O6,
  output O7
);

  D_Flip_Flop d_ff_1 (.clk(CLK), .D(I1), .Q(O1), .preset(1'b0), .en(Enable), .reset(1'b0));  // open: Qn
  D_Flip_Flop d_ff_2 (.clk(CLK), .D(I2), .Q(O2), .preset(1'b0), .en(Enable), .reset(1'b0));  // open: Qn
  D_Flip_Flop d_ff_3 (.clk(CLK), .D(I3), .Q(O3), .preset(1'b0), .en(Enable), .reset(1'b0));  // open: Qn
  D_Flip_Flop d_ff_4 (.clk(CLK), .D(I4), .Q(O4), .preset(1'b0), .en(Enable), .reset(1'b0));  // open: Qn
  D_Flip_Flop d_ff_5 (.clk(CLK), .D(I5), .Q(O5), .preset(1'b0), .en(Enable), .reset(1'b0));  // open: Qn
  D_Flip_Flop d_ff_6 (.clk(CLK), .D(I6), .Q(O6), .preset(1'b0), .en(Enable), .reset(1'b0));  // open: Qn
  D_Flip_Flop d_ff_7 (.clk(CLK), .D(I7), .Q(O7), .preset(1'b0), .en(Enable), .reset(1'b0));  // open: Qn
endmodule
