// Logisim project serialbcd (1).circ as structural Verilog: 2 circuits, main circuit main
module main (
  input  in_1,
  input  I_lsb,
  input  I_msb,
  input  in_4,
  input  clock,
  input  reset,
  output O_msb,
  output out_8,
  output out_9,
  output O_lsb
);

  wire decoder_1_out10, decoder_1_out11, decoder_1_out12, decoder_1_out13, decoder_1_out14, decoder_1_out15,
       decoder_2_out1, decoder_2_out2, decoder_2_out3, decoder_2_out4, decoder_2_out5, decoder_2_out6,
       decoder_2_out7, decoder_2_out8, decoder_2_out9, decoder_2_out10, or_1_out, or_2_out, or_3_out,
       or_4_out, or_5_out;
  wire [3:0] multiplexer_1_out;

  Decoder #(.select(4)) decoder_1 (
    .out10(decoder_1_out10), .out11(decoder_1_out11), .out12(decoder_1_out12), .out13(decoder_1_out13),
    .out14(decoder_1_out14), .out15(decoder_1_out15), .sel({O_msb, out_8, out_9, O_lsb}));  // open: out0, out1, out2, out3, out4, out5, out6, out7, out8, out9, en
  Multiplexer #(.width(4), .disabled(0), .enable("false")) multiplexer_1 (
    .in0({I_msb, in_4, in_1, I_lsb}), .in1({I_msb, in_4, in_1, I_lsb}), .out(multiplexer_1_out),
    .sel(or_1_out));
  Pull_Resistor pull_resistor_1 ();  // open: node
  or or_1 (or_1_out, decoder_1_out10, decoder_1_out11, decoder_1_out12, decoder_1_out13, decoder_1_out14, decoder_1_out15);
  Pull_Resistor pull_resistor_2 (.node(I_msb));
  Pull_Resistor pull_resistor_3 (.node(in_4));
  Decoder #(.select(4)) decoder_2 (
    .out1(decoder_2_out1), .out2(decoder_2_out2), .out3(decoder_2_out3), .out4(decoder_2_out4),
    .out5(decoder_2_out5), .out6(decoder_2_out6), .out7(decoder_2_out7), .out8(decoder_2_out8),
    .out9(decoder_2_out9), .out10(decoder_2_out10), .out11(decoder_2_out10), .out12(decoder_2_out10),
    .out13(decoder_2_out10), .out14(decoder_2_out10), .out15(decoder_2_out10), .sel(multiplexer_1_out));  // open: out0, en
  or or_2 (or_2_out, decoder_2_out9, decoder_2_out8, decoder_2_out7, decoder_2_out6, decoder_2_out5);
  D_Flip_Flop d_ff_1 (.clk(clock), .D(or_2_out), .Q(O_msb), .reset(reset));  // open: Qn, preset, en
  Pull_Resistor pull_resistor_4 (.node(in_1));
  or or_3 (or_3_out, decoder_2_out4, decoder_2_out9);
  D_Flip_Flop d_ff_2 (.clk(clock), .D(or_3_out), .Q(out_8), .reset(reset));  // open: Qn, preset, en
  or or_4 (or_4_out, decoder_2_out8, decoder_2_out7, decoder_2_out3, decoder_2_out2);
  D_Flip_Flop d_ff_3 (.clk(clock), .D(or_4_out), .Q(out_9), .reset(reset));  // open: Qn, preset, en
  or or_5 (or_5_out, decoder_2_out8, decoder_2_out6, decoder_2_out3, decoder_2_out1);
  D_Flip_Flop d_ff_4 (.clk(clock), .D(or_5_out), .Q(O_lsb), .reset(reset));  // open: Qn, preset, en
endmodule

module serialbcd (
  input  [7:0] B,
  input  reset
);

  wire and_1_out, clock_1_out, counter_1_carry, main_1_o_lsb, main_1_out_8, main_1_out_9, main_2_o_lsb,
       main_2_o_msb, main_2_out_8, main_2_out_9, main_3_o_lsb, main_3_o_msb, main_3_out_8, main_3_out_9,
       multiplexer_1_out;
  wire [2:0] counter_1_q;

  main main_1 (
    .I_msb(main_1_out_8), .in_4(main_1_out_9), .in_1(main_1_o_lsb), .I_lsb(main_2_o_msb),
    .out_8(main_1_out_8), .out_9(main_1_out_9), .O_lsb(main_1_o_lsb), .clock(and_1_out), .reset(reset));  // open: O_msb
  main main_2 (
    .I_msb(main_2_out_8), .in_4(main_2_out_9), .in_1(main_2_o_lsb), .I_lsb(main_3_o_msb),
    .O_msb(main_2_o_msb), .out_8(main_2_out_8), .out_9(main_2_out_9), .O_lsb(main_2_o_lsb),
    .clock(and_1_out), .reset(reset));
  Multiplexer #(.select(3)) multiplexer_1 (
    .in0(B[7]), .in1(B[6]), .in2(B[5]), .in3(B[4]), .in4(B[3]), .in5(B[2]), .in6(B[1]), .in7(B[0]),
    .out(multiplexer_1_out), .sel(counter_1_q), .en(1'b1));
  main main_3 (
    .I_msb(main_3_out_8), .in_4(main_3_out_9), .in_1(main_3_o_lsb), .I_lsb(multiplexer_1_out),
    .O_msb(main_3_o_msb), .out_8(main_3_out_8), .out_9(main_3_out_9), .O_lsb(main_3_o_lsb),
    .clock(and_1_out), .reset(reset));
  Clock clock_1 (.out(clock_1_out));
  and and_1 (and_1_out, clock_1_out, ~counter_1_carry);  // AND_Gate
  Counter #(.width(3), .max('h7)) counter_1 (
    .count(1'b1), .Q(counter_1_q), .carry(counter_1_carry), .clk(and_1_out), .clr(reset));  // open: load, D
endmodule
